// Digital circuit DCOUTER.dig as structural Verilog
module DCOUTER (
  input  CLK,
  input  nCLR,
  input  CNT,
  input  nLE,
  input  [11:0] D,
  output [11:0] Q
);

  CounterPreset #(.Bits(12)) counterpreset_1 (
    .en(CNT), .C(CLK), .dir(1'b0), .in(D), .ld(~nLE), .clr(~nCLR), .out(Q));  // open: ovf

  // Notes on the sheet:
  //   CNT: Q = Q + 1, lower priority than LE
  //   nLE: load value from D
endmodule
