// Digital circuit PER_INT_IO.dig as structural Verilog
// interrupt, IO:
// UART: SBUF, SCON
// external int: TCON
module PER_INT_IO (
  input  CLK,
  input  nRST,
  input  [7:0] A,
  input  [7:0] D,
  input  nWE,
  input  nOE,
  input  IRR_CLR,
  input  nIRR_OE,
  output [7:0] IRR_Q
);

  wire RST, SBUF_ri, SBUF_ti, SFR_OE, SFR_WE;
  wire [7:0] clrirr_1_q;

  CLRIRR clrirr_1 (.D(D), .IRR_CLR(IRR_CLR), .Q(clrirr_1_q));
  not not_1 (RST, nRST);
  not not_2 (SFR_WE, nWE);
  not not_3 (SFR_OE, nOE);
  SBUF SBUF (.IO(D), .CLK(CLK), .A(A), .OE(SFR_OE), .WE(SFR_WE), .RI(SBUF_ri), .TI(SBUF_ti));
  SFR_TCON sfr_tcon_1 (
    .D(D), .CLK(CLK), .nRST(nRST), .IRQ(4'b0000), .nIRR_CB(clrirr_1_q[3:0]), .nWE(nWE), .nOE(nOE), .A(A),
    .MADDR(8'h88), .IRRQ(IRR_Q[3:0]));  // open: Q
  SCON scon_1 (
    .CLK(CLK), .CLR(RST), .IO(D), .A(A), .OE(SFR_OE), .WE(SFR_WE), .RI(SBUF_ri), .TI(SBUF_ti), .TRI(IRR_Q[4]));
  assign D = ~nIRR_OE ? {3'b000, IRR_Q[4:0]} : 8'bz;  // DriverInvSel driverinvsel_1

  assign IRR_Q[7:5] = 3'b000;

  // Other names for the same wires on the sheet: ADDR_SFR[7:0] = A; BUS_D[7:0] = D; nSFR_OE = nOE; nSFR_WE = nWE

  // Notes on the sheet:
  //   nRST: default 1
  //   A: address input
  //   D: Data Bus
  //   nWE: write enable
  //   The SFR in the corresponding address will read the data from  the data bus., default 1
  //   nOE: ouput enable.
  //   The SFR in the corresponding address will drive the data  bus., default 1
  //   nIRR_OE: IRR ouput enable.
  //   The IRR will drive the data bus., default 1
endmodule
