// Digital circuit TOP.dig as structural Verilog
module TOP (
  input  clk,
  input  [11:0] MIPCBI,
  input  MIPCBE,
  input  [15:0] PCBIA1,
  input  PCBE1,
  input  [15:0] PCBIA2,
  input  PCBE2
);

  wire and_1_out, and_2_out, and_3_out, AST_FAIL, button_2_out, button_3_out, button_4_out, CLK_t, CLR,
       comparator_1_eq, comparator_2_eq, comparator_3_eq, core_1_p17, core_1_p18, dipswitch_1_out, DUMP_p5,
       EXIT_p5, IRQ_CAI, nIRQ_OE, nXRAM_OE, nXRAM_WE, or_1_out, RI, SFR_OE, SFR_WE, TI;
  wire [7:0] ADDR_SFR, ADDR_XRAM, BUS_D, INT_irq;
  wire [11:0] MIPC;
  wire [15:0] PC;

  // Probe on PC
  // Probe on MIPC
  Button button_1 (.out(CLR));
  RAMSinglePortSel #(.AddrBits(16), .isProgramMemory("true"), .Bits(8)) XRAM (
    .A({ADDR_SFR, ADDR_XRAM}), .CS(~1'b0), .WE(~nXRAM_WE), .OE(~nXRAM_OE), .D(BUS_D));
  Comparator #(.Bits(12)) comparator_1 (.a(MIPCBI), .b(MIPC), .eq(comparator_1_eq));  // open: gt, lt
  Comparator #(.Bits(16)) comparator_2 (.a(PCBIA1), .b(PC), .eq(comparator_2_eq));  // open: gt, lt
  Comparator #(.Bits(16)) comparator_3 (.a(PCBIA2), .b(PC), .eq(comparator_3_eq));  // open: gt, lt
  and and_1 (and_1_out, comparator_1_eq, MIPCBE);
  and and_2 (and_2_out, comparator_2_eq, PCBE1);
  and and_3 (and_3_out, comparator_3_eq, PCBE2);
  SBUF SBUF (.IO(BUS_D), .CLK(CLK_t), .A(ADDR_SFR), .OE(SFR_OE), .WE(SFR_WE), .RI(RI), .TI(TI));
  DipSwitch dipswitch_1 (.out(dipswitch_1_out));
  Button button_2 (.out(button_2_out));
  Button button_3 (.out(button_3_out));
  Button button_4 (.out(button_4_out));
  or or_1 (or_1_out, and_1_out, and_2_out, and_3_out, AST_FAIL);
  // CORE core_1: pin names not known; wires that end beside it: clk, button_2_out, dipswitch_1_out, button_3_out, button_4_out, CLR, or_1_out, PC, MIPC, BUS_D, {ADDR_SFR, ADDR_XRAM}, nXRAM_WE, nXRAM_OE, CLK_t, nIRQ_OE, IRQ_CAI, core_1_p17, core_1_p18
  INT INT (
    .CLK(CLK_t), .CLR(CLR), .A(ADDR_SFR), .D(BUS_D), .WE(SFR_WE), .OE(SFR_OE), .IRQOE(nIRQ_OE),
    .CAI(IRQ_CAI), .RI(RI), .TI(TI), .IRQ(INT_irq));
  // ASSERT ASSERT: pin names not known; wires that end beside it: CLK_t, BUS_D, ADDR_SFR, SFR_WE, AST_FAIL
  not not_1 (SFR_WE, core_1_p17);
  not not_2 (SFR_OE, core_1_p18);
  // Probe on INT_irq
  // EXTCTL EXIT: pin names not known; wires that end beside it: SFR_WE, ADDR_SFR, BUS_D, CLK_t, EXIT_p5
  // Probe on EXIT_p5
  // DUMP DUMP: pin names not known; wires that end beside it: SFR_WE, ADDR_SFR, BUS_D, CLK_t, DUMP_p5
  // Probe on DUMP_p5

  // Other names for the same wires on the sheet: ADDR_XRAM[15:8] = ADDR_SFR

  // Notes on the sheet:
  //   clk: Hz: 2147483647
  //   MIPCBI: default 1291
  //   PCBIA1: default 1398
  //   contents of ROM (hex, n*v repeats v):
  //   2,0,58,12,0,1f,22,0,0,0,0,12,0,2d,22,0,0,0,0,12,0,3b,22,0,0,0,0,12,0,49,22,24,1,a8, 81,18,86,
  //   f0,15,f0,15,f0,15,f0,22,24,2,a8,81,18,86,f0,15,f0,15,f0,15,f0,22,24,3,a8, 81,18,86,f0,15,f0,
  //   15,f0,15,f0,22,24,4,a8,81,18,86,f0,15,f0,15,f0,15,f0,22,32,75,81, 0,75,82,0,75,83,0,75,d0,0,
  //   75,e0,0,75,f0,0,75,d0,0,75,0,ff,76,0,75,0,fe,76,0,75,0, fd,76,0,75,0,fc,76,0,75,0,fb,76,0,75,
  //   0,fa,76,0,75,0,f9,76,0,75,0,f8,76,0,75,0,f7, 76,0,75,0,f6,76,0,75,0,f5,76,0,75,0,f4,76,0,75,
  //   0,f3,76,0,75,0,f2,76,0,75,0,f1,76, 0,75,0,f0,76,0,75,0,ef,76,0,75,0,ee,76,0,75,0,ed,76,0,75,
  //   0,ec,76,0,75,0,eb,76,0,75, 0,ea,76,0,75,0,e9,76,0,75,0,e8,76,0,75,0,e7,76,0,75,0,e6,76,0,75,
  //   0,e5,76,0,75,0,e4, 76,0,75,0,e3,76,0,75,0,e2,76,0,75,0,e1,76,0,75,0,e0,76,0,75,0,df,76,0,75,
  //   0,de,76, 0,75,0,dd,76,0,75,0,dc,76,0,75,0,db,76,0,75,0,da,76,0,75,0,d9,76,0,75,0,d8,76,0,75,
  //    0,d7,76,0,75,0,d6,76,0,75,0,d5,76,0,75,0,d4,76,0,75,0,d3,76,0,75,0,d2,76,0,75,0,d1, 76,0,75,
  //   0,d0,76,0,75,0,cf,76,0,75,0,ce,76,0,75,0,cd,76,0,75,0,cc,76,0,75,0,cb,76, 0,75,0,ca,76,0,75,
  //   0,c9,76,0,75,0,c8,76,0,75,0,c7,76,0,75,0,c6,76,0,75,0,c5,76,0,75, 0,c4,76,0,75,0,c3,76,0,75,
  //   0,c2,76,0,75,0,c1,76,0,75,0,c0,76,0,75,0,bf,76,0,75,0,be, 76,0,75,0,bd,76,0,75,0,bc,76,0,75,
  //   0,bb,76,0,75,0,ba,76,0,75,0,b9,76,0,75,0,b8,76, 0,75,0,b7,76,0,75,0,b6,76,0,75,0,b5,76,0,75,
  //   0,b4,76,0,75,0,b3,76,0,75,0,b2,76,0,75, 0,b1,76,0,75,0,b0,76,0,75,0,af,76,0,75,0,ae,76,0,75,
  //   0,ad,76,0,75,0,ac,76,0,75,0,ab, 76,0,75,0,aa,76,0,75,0,a9,76,0,75,0,a8,76,0,75,0,a7,76,0,75,
  //   0,a6,76,0,75,0,a5,76, 0,75,0,a4,76,0,75,0,a3,76,0,75,0,a2,76,0,75,0,a1,76,0,75,0,a0,76,0,75,
  //   0,9f,76,0,75, 0,9e,76,0,75,0,9d,76,0,75,0,9c,76,0,75,0,9b,76,0,75,0,9a,76,0,75,0,99,76,0,75,
  //   0,98, 76,0,75,0,97,76,0,75,0,96,76,0,75,0,95,76,0,75,0,94,76,0,75,0,93,76,0,75,0,92,76, 0,75,
  //   0,91,76,0,75,0,90,76,0,75,0,8f,76,0,75,0,8e,76,0,75,0,8d,76,0,75,0,8c,76,0,75, 0,8b,76,0,75,
  //   0,8a,76,0,75,0,89,76,0,75,0,88,76,0,75,0,87,76,0,75,0,86,76,0,75,0,85, 76,0,75,0,84,76,0,75,
  //   0,83,76,0,75,0,82,76,0,75,0,81,76,0,75,0,80,76,0,75,0,7f,76, 0,75,0,7e,76,0,75,0,7d,76,0,75,
  //   0,7c,76,0,75,0,7b,76,0,75,0,7a,76,0,75,0,79,76,0,75, 0,78,76,0,75,0,77,76,0,75,0,76,76,0,75,
  //   0,75,76,0,75,0,74,76,0,75,0,73,76,0,75,0,72, 76,0,75,0,71,76,0,75,0,70,76,0,75,0,6f,76,0,75,
  //   0,6e,76,0,75,0,6d,76,0,75,0,6c,76, 0,75,0,6b,76,0,75,0,6a,76,0,75,0,69,76,0,75,0,68,76,0,75,
  //   0,67,76,0,75,0,66,76,0,75, 0,65,76,0,75,0,64,76,0,75,0,63,76,0,75,0,62,76,0,75,0,61,76,0,75,
  //   0,60,76,0,75,0,5f, 76,0,75,0,5e,76,0,75,0,5d,76,0,75,0,5c,76,0,75,0,5b,76,0,75,0,5a,76,0,75,
  //   0,59,76, 0,75,0,58,76,0,75,0,57,76,0,75,0,56,76,0,75,0,55,76,0,75,0,54,76,0,75,0,53,76,0,75,
  //    0,52,76,0,75,0,51,76,0,75,0,50,76,0,75,0,4f,76,0,75,0,4e,76,0,75,0,4d,76,0,75,0,4c, 76,0,75,
  //   0,4b,76,0,75,0,4a,76,0,75,0,49,76,0,75,0,48,76,0,75,0,47,76,0,75,0,46,76, 0,75,0,45,76,0,75,
  //   0,44,76,0,75,0,43,76,0,75,0,42,76,0,75,0,41,76,0,75,0,40,76,0,75, 0,3f,76,0,75,0,3e,76,0,75,
  //   0,3d,76,0,75,0,3c,76,0,75,0,3b,76,0,75,0,3a,76,0,75,0,39, 76,0,75,0,38,76,0,75,0,37,76,0,75,
  //   0,36,76,0,75,0,35,76,0,75,0,34,76,0,75,0,33,76, 0,75,0,32,76,0,75,0,31,76,0,75,0,30,76,0,75,
  //   0,2f,76,0,75,0,2e,76,0,75,0,2d,76,0,75, 0,2c,76,0,75,0,2b,76,0,75,0,2a,76,0,75,0,29,76,0,75,
  //   0,28,76,0,75,0,27,76,0,75,0,26, 76,0,75,0,25,76,0,75,0,24,76,0,75,0,23,76,0,75,0,22,76,0,75,
  //   0,21,76,0,75,0,20,76, 0,75,0,1f,76,0,75,0,1e,76,0,75,0,1d,76,0,75,0,1c,76,0,75,0,1b,76,0,75,
  //   0,1a,76,0,75, 0,19,76,0,75,0,18,76,0,75,0,17,76,0,75,0,16,76,0,75,0,15,76,0,75,0,14,76,0,75,
  //   0,13, 76,0,75,0,12,76,0,75,0,11,76,0,75,0,10,76,0,75,0,f,76,0,75,0,e,76,0,75,0,d,76,0,75, 0,
  //   c,76,0,75,0,b,76,0,75,0,a,76,0,75,0,9,76,0,75,0,8,76,0,75,0,7,76,0,75,0,6,76,0, 75,0,5,76,0,
  //   75,0,4,76,0,75,0,3,76,0,75,0,2,76,0,75,0,1,76,0,75,0,0,76,0,75,a8,8f, 75,88,5,53,b8,fe,43,88,
  //   2,75,f0,0,53,b8,fe,43,88,2,53,88,fd,85,e0,fd,75,fe,1,75,ff, 2,75,f0,0,43,b8,1,43,88,2,85,f0,
  //   fd,75,fe,3,75,ff,2,85,88,f0,53,f0,2,85,f0,fd,75,fe, 0,75,ff,2,85,e0,fd,75,fe,2,75,ff,2,12,0,
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  //   contents of ALUDL (hex, n*v repeats v):
  //   10,21,42,83,4,5,6,7,18,29,4a,8b,c,d,e,f,1,30,53,92,15,14,17,16,9,38,5b,9a,1d,1c,1f, 1e,32,3,
  //   60,a1,26,27,24,25,3a,b,68,a9,2e,2f,2c,2d,23,12,71,b0,37,36,35,34,2b,1a,79, b8,3f,3e,3d,3c,54,
  //   65,6,c7,40,41,42,43,5c,6d,e,cf,48,49,4a,4b,45,74,17,d6,51,50,53, 52,4d,7c,1f,de,59,58,5b,5a,
  //   76,47,24,e5,62,63,60,61,7e,4f,2c,ed,6a,6b,68,69,67,56, 35,f4,73,72,71,70,6f,5e,3d,fc,7b,7a,
  //   79,78,98,a9,ca,b,8c,8d,8e,8f,90,a1,c2,3,84,85, 86,87,89,b8,db,1a,9d,9c,9f,9e,81,b0,d3,12,95,
  //   94,97,96,ba,8b,e8,29,ae,af,ac,ad,b2, 83,e0,21,a6,a7,a4,a5,ab,9a,f9,38,bf,be,bd,bc,a3,92,f1,
  //   30,b7,b6,b5,b4,dc,ed,8e,4f, c8,c9,ca,cb,d4,e5,86,47,c0,c1,c2,c3,cd,fc,9f,5e,d9,d8,db,da,c5,
  //   f4,97,56,d1,d0,d3, d2,fe,cf,ac,6d,ea,eb,e8,e9,f6,c7,a4,65,e2,e3,e0,e1,ef,de,bd,7c,fb,fa,f9,
  //   f8,e7,d6, b5,74,f3,f2,f1,f0,0,1,2,3,4,5,6,7,8,9,80,81,82,83,84,85,0,1,2,3,4,5,6,7,8,9,80,81,
  //    82,83,84,85,0,1,2,3,4,5,6,7,8,9,80,81,82,83,84,85,0,1,2,3,4,5,6,7,8,9,80,81,82,83, 84,85,0,
  //   1,2,3,4,5,6,7,8,9,80,81,82,83,84,85,0,1,2,3,4,5,6,7,8,9,80,81,82,83,84,85, 0,1,2,3,4,5,6,7,
  //   8,9,80,81,82,83,84,85,0,1,2,3,4,5,6,7,8,9,80,81,82,83,84,85,6,7,48, 49,4a,4b,4c,4d,e,f,80,81,
  //   82,83,84,85,6,7,48,49,4a,4b,4c,4d,e,f,80,81,82,83,84,85, 6,7,48,49,4a,4b,4c,4d,e,f,80,81,82,
  //   83,84,85,6,7,48,49,4a,4b,4c,4d,e,f,80,81,82,83, 84,85,6,7,48,49,4a,4b,4c,4d,e,f,80,81,82,83,
  //   84,85,6,7,48,49,4a,4b,4c,4d,e,f,80,81, 82,83,84,85,6,7,48,49,4a,4b,4c,4d,e,f,80,81,82,83,84,
  //   85,6,7,48,49,4a,4b,4c,4d,e,f, 80,81,82,83,84,85,0,1,2,3,4,5,6,7,8,9,a,b,c,d,e,f,1,2,3,4,5,6,
  //   7,48,9,a,b,c,d,e,f, 80,2,3,4,5,6,7,48,49,a,b,c,d,e,f,80,81,3,4,5,6,7,48,49,4a,b,c,d,e,f,80,
  //   81,82,4,5, 6,7,48,49,4a,4b,c,d,e,f,80,81,82,83,5,6,7,48,49,4a,4b,4c,d,e,f,80,81,82,83,84,6,
  //   7, 48,49,4a,4b,4c,4d,e,f,80,81,82,83,84,85,7,48,49,4a,4b,4c,4d,4e,f,80,81,82,83,84,85, 86,8,
  //   9,a,b,c,d,e,f,c0,c1,c2,c3,c4,c5,c6,c7,9,a,b,c,d,e,f,80,c1,c2,c3,c4,c5,c6,c7, 88,a,b,c,d,e,f,
  //   80,81,c2,c3,c4,c5,c6,c7,88,89,b,c,d,e,f,80,81,82,c3,c4,c5,c6,c7,88, 89,8a,c,d,e,f,80,81,82,
  //   83,c4,c5,c6,c7,88,89,8a,8b,d,e,f,80,81,82,83,84,c5,c6,c7,88, 89,8a,8b,8c,e,f,80,81,82,83,84,
  //   85,c6,c7,88,89,8a,8b,8c,8d,f,80,81,82,83,84,85,86, c7,88,89,8a,8b,8c,8d,8e,0,1,2,3,4,5,6,7,
  //   8,9,a,b,c,d,e,f,8f,0,1,2,3,4,5,6,47,8,9,a, b,c,d,e,8e,8f,0,1,2,3,4,5,46,47,8,9,a,b,c,d,8d,8e,
  //   8f,0,1,2,3,4,45,46,47,8,9,a,b,c, 8c,8d,8e,8f,0,1,2,3,44,45,46,47,8,9,a,b,8b,8c,8d,8e,8f,0,1,
  //   2,43,44,45,46,47,8,9,a, 8a,8b,8c,8d,8e,8f,0,1,42,43,44,45,46,47,8,9,89,8a,8b,8c,8d,8e,8f,0,
  //   41,42,43,44,45, 46,47,8,c8,c9,ca,cb,cc,cd,ce,cf,0,1,2,3,4,5,6,7,87,c8,c9,ca,cb,cc,cd,ce,8f,
  //   0,1,2, 3,4,5,6,86,87,c8,c9,ca,cb,cc,cd,8e,8f,0,1,2,3,4,5,85,86,87,c8,c9,ca,cb,cc,8d,8e,8f, 0,
  //   1,2,3,4,84,85,86,87,c8,c9,ca,cb,8c,8d,8e,8f,0,1,2,3,83,84,85,86,87,c8,c9,ca,8b, 8c,8d,8e,8f,
  //   0,1,2,82,83,84,85,86,87,c8,c9,8a,8b,8c,8d,8e,8f,0,1,81,82,83,84,85,86, 87,c8,89,8a,8b,8c,8d,
  //   8e,8f,0,0,81,82,3,84,5,6,87,88,9,a,8b,c,8d,8e,f,0,81,82,3,84, 5,6,87,88,9,a,8b,c,8d,8e,f,0,
  //   81,82,3,84,5,6,87,88,9,a,8b,c,8d,8e,f,0,81,82,3,84,5, 6,87,88,9,a,8b,c,8d,8e,f,0,81,82,3,84,
  //   5,6,87,88,9,a,8b,c,8d,8e,f,0,81,82,3,84,5,6, 87,88,9,a,8b,c,8d,8e,f,0,81,82,3,84,5,6,87,88,
  //   9,a,8b,c,8d,8e,f,0,81,82,3,84,5,6,87, 88,9,a,8b,c,8d,8e,f,0,81,82,3,84,5,6,87,88,9,a,8b,c,8d,
  //   8e,f,0,81,82,3,84,5,6,87,88, 9,a,8b,c,8d,8e,f,0,81,82,3,84,5,6,87,88,9,a,8b,c,8d,8e,f,0,81,
  //   82,3,84,5,6,87,88,9, a,8b,c,8d,8e,f,0,81,82,3,84,5,6,87,88,9,a,8b,c,8d,8e,f,0,81,82,3,84,5,
  //   6,87,88,9,a, 8b,c,8d,8e,f,0,81,82,3,84,5,6,87,88,9,a,8b,c,8d,8e,f,0,81,82,3,84,5,6,87,88,9,
  //   a,8b, c,8d,8e,f,0,11,20,31,40,51,60,71,80,91,a0,b1,c0,d1,e0,f1,10,11,30,31,50,51,70,71, 90,
  //   91,b0,b1,d0,d1,f0,f1,20,31,20,31,60,71,60,71,a0,b1,a0,b1,e0,f1,e0,f1,30,31,30, 31,70,71,70,
  //   71,b0,b1,b0,b1,f0,f1,f0,f1,40,51,60,71,40,51,60,71,c0,d1,e0,f1,c0,d1, e0,f1,50,51,70,71,50,
  //   51,70,71,d0,d1,f0,f1,d0,d1,f0,f1,60,71,60,71,60,71,60,71,e0, f1,e0,f1,e0,f1,e0,f1,70,71,70,
  //   71,70,71,70,71,f0,f1,f0,f1,f0,f1,f0,f1,88,99,a8,b9, c8,d9,e8,f9,88,99,a8,b9,c8,d9,e8,f9,98,
  //   99,b8,b9,d8,d9,f8,f9,98,99,b8,b9,d8,d9,f8, f9,a8,b9,a8,b9,e8,f9,e8,f9,a8,b9,a8,b9,e8,f9,e8,
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  //   contents of ALUS (hex, n*v repeats v):
  //   0,1,2,3,4,5,6,7,40,41,42,43,44,45,46,47,10,11,12,13,14,15,16,17,50,51,52,53,54,55, 56,57,20,
  //   21,22,23,24,25,26,27,60,61,62,63,64,65,66,67,30,31,32,33,34,35,36,37,70, 71,72,73,74,75,76,
  //   77,8,9,a,b,c,d,e,f,48,49,4a,4b,4c,4d,4e,4f,18,19,1a,1b,1c,1d,1e, 1f,58,59,5a,5b,5c,5d,5e,5f,
  //   28,29,2a,2b,2c,2d,2e,2f,68,69,6a,6b,6c,6d,6e,6f,38,39, 3a,3b,3c,3d,3e,3f,78,79,7a,7b,7c,7d,
  //   7e,7f,80,81,82,83,84,85,86,87,c0,c1,c2,c3,c4, c5,c6,c7,90,91,92,93,94,95,96,97,d0,d1,d2,d3,
  //   d4,d5,d6,d7,a0,a1,a2,a3,a4,a5,a6,a7, e0,e1,e2,e3,e4,e5,e6,e7,b0,b1,b2,b3,b4,b5,b6,b7,f0,f1,
  //   f2,f3,f4,f5,f6,f7,88,89,8a, 8b,8c,8d,8e,8f,c8,c9,ca,cb,cc,cd,ce,cf,98,99,9a,9b,9c,9d,9e,9f,
  //   d8,d9,da,db,dc,dd, de,df,a8,a9,aa,ab,ac,ad,ae,af,e8,e9,ea,eb,ec,ed,ee,ef,b8,b9,ba,bb,bc,bd,
  //   be,bf,f8, f9,fa,fb,fc,fd,fe,ff,fb,3,b,3,13,3,b,3,1b,3,b,3,13,3,b,3,23,3,b,3,13,3,b,3,1b,3,b,
  //    3,13,3,b,3,2b,3,b,3,13,3,b,3,1b,3,b,3,13,3,b,3,23,3,b,3,13,3,b,3,1b,3,b,3,13,3,b, 3,33,3,b,
  //   3,13,3,b,3,1b,3,b,3,13,3,b,3,23,3,b,3,13,3,b,3,1b,3,b,3,13,3,b,3,2b,3,b, 3,13,3,b,3,1b,3,b,
  //   3,13,3,b,3,23,3,b,3,13,3,b,3,1b,3,b,3,13,3,b,3,3b,3,b,3,13,3,b, 3,1b,3,b,3,13,3,b,3,23,3,b,
  //   3,13,3,b,3,1b,3,b,3,13,3,b,3,2b,3,b,3,13,3,b,3,1b,3,b, 3,13,3,b,3,23,3,b,3,13,3,b,3,1b,3,b,
  //   3,13,3,b,3,33,3,b,3,13,3,b,3,1b,3,b,3,13,3,b, 3,23,3,b,3,13,3,b,3,1b,3,b,3,13,3,b,3,2b,3,b,
  //   3,13,3,b,3,1b,3,b,3,13,3,b,3,23,3,b, 3,13,3,b,3,1b,3,b,3,13,3,b,3,0,0,0,0,0,0,0,0,0,0,0,0,0,
  //   0,0,0,0,0,0,0,0,0,0,0,0,0, 0,0,0,0,0,0,0,0,0,0,0,0,0,0,0,0,0,0,0,0,0,0,0,0,0,0,0,0,0,0,0,0,
  //   0,0,0,0,0,0,0,0,0, 0,0,0,0,0,0,0,0,0,0,0,0,0,0,0,0,0,0,0,0,0,0,0,0,0,0,0,0,0,0,0,0,0,0,0,0,
  //   0,0,0,0,0, 0,0,0,0,0,0,0,0,0,0,0,0,0,0,0,0,0,0,0,0,0,0,0,0,0,0,0,0,0,0,0,0,0,0,0,0,0,0,0,0,
  //   0, 0,0,0,0,0,0,0,0,0,0,0,0,0,0,0,0,0,0,0,0,0,0,0,0,0,0,0,0,0,0,0,0,0,0,0,0,0,0,0,0,0, 0,0,0,
  //   0,0,0,0,0,0,0,0,0,0,0,0,0,0,0,0,0,0,0,0,0,0,0,0,0,0,0,0,0,0,0,0,0,0,0,0,0,0, 0,0,0,0,0,0,0,
  //   0,0,0,0,0,0,0,0,0,0,0,0,0,0,0,0,0,0,0,0,0,0,0,0,0,0,0,0,0,0,0,0,0,0, 0,0,0,0,0,0,0,0,0,0,0,
  //   0,0,0,0,0,0,0,0,0,0,0,0,0,0,0,0,0,0,0,0,0,0,0,0,0,0,0,0,0,0, 0,0,0,0,0,0,0,0,0,0,0,0,0,0,0,
  //   0,0,0,0,0,0,0,0,0,0,0,0,0,0,0,0,0,0,0,0,0,0,0,0,0,0, 0,0,0,0,0,0,0,0,0,0,0,0,0,0,0,0,0,0,0,
  //   0,0,0,0,0,0,0,0,0,0,0,0,8,9,a,0,0,0,0,0,0,0, 0,0,0,0,0,0,0,0,0,0,0,0,0,0,0,0,0,0,0,0,0,0,0,
  //   0,0,0,0,0,0,b,0,0,0,0,0,0,0,0,0,0,0, 0,0,0,0,c,0,0,0,0,0,0,0,0,0,0,0,0,0,0,0,0,0,0,0,0,0,0,
  //   0,d,0,0,0,0,0,0,0,0,0,0,0,0, 0,0,0,e,0,0,0,0,0,0,0,0,0,0,0,0,0,0,0,f,0,0,0,0,0,0,0,0,0,0,0,
  //   0,0,0,0,0,80,1,81,2, 82,3,83,4,84,5,85,6,86,7,87,8,88,9,89,a,8a,b,8b,c,8c,d,8d,e,8e,f,8f,10,
  //   90,11,91,12, 92,13,93,14,94,15,95,16,96,17,97,18,98,19,99,1a,9a,1b,9b,1c,9c,1d,9d,1e,9e,1f,
  //   9f, 20,a0,21,a1,22,a2,23,a3,24,a4,25,a5,26,a6,27,a7,28,a8,29,a9,2a,aa,2b,ab,2c,ac,2d, ad,2e,
  //   ae,2f,af,30,b0,31,b1,32,b2,33,b3,34,b4,35,b5,36,b6,37,b7,38,b8,39,b9,3a,ba, 3b,bb,3c,bc,3d,
  //   bd,3e,be,3f,bf,40,c0,41,c1,42,c2,43,c3,44,c4,45,c5,46,c6,47,c7,48, c8,49,c9,4a,ca,4b,cb,4c,
  //   cc,4d,cd,4e,ce,4f,cf,50,d0,51,d1,52,d2,53,d3,54,d4,55,d5, 56,d6,57,d7,58,d8,59,d9,5a,da,5b,
  //   db,5c,dc,5d,dd,5e,de,5f,df,60,e0,61,e1,62,e2,63, e3,64,e4,65,e5,66,e6,67,e7,68,e8,69,e9,6a,
  //   ea,6b,eb,6c,ec,6d,ed,6e,ee,6f,ef,70,f0, 71,f1,72,f2,73,f3,74,f4,75,f5,76,f6,77,f7,78,f8,79,
  //   f9,7a,fa,7b,fb,7c,fc,7d,fd,7e, fe,7f,ff,0,2,4,6,8,a,c,e,10,12,14,16,18,1a,1c,1e,20,22,24,26,
  //   28,2a,2c,2e,30,32,34, 36,38,3a,3c,3e,40,42,44,46,48,4a,4c,4e,50,52,54,56,58,5a,5c,5e,60,62,
  //   64,66,68,6a, 6c,6e,70,72,74,76,78,7a,7c,7e,80,82,84,86,88,8a,8c,8e,90,92,94,96,98,9a,9c,9e,
  //   a0, a2,a4,a6,a8,aa,ac,ae,b0,b2,b4,b6,b8,ba,bc,be,c0,c2,c4,c6,c8,ca,cc,ce,d0,d2,d4,d6, d8,da,
  //   dc,de,e0,e2,e4,e6,e8,ea,ec,ee,f0,f2,f4,f6,f8,fa,fc,fe,1,3,5,7,9,b,d,f,11,13, 15,17,19,1b,1d,
  //   1f,21,23,25,27,29,2b,2d,2f,31,33,35,37,39,3b,3d,3f,41,43,45,47,49, 4b,4d,4f,51,53,55,57,59,
  //   5b,5d,5f,61,63,65,67,69,6b,6d,6f,71,73,75,77,79,7b,7d,7f, 81,83,85,87,89,8b,8d,8f,91,93,95,
  //   97,99,9b,9d,9f,a1,a3,a5,a7,a9,ab,ad,af,b1,b3,b5, b7,b9,bb,bd,bf,c1,c3,c5,c7,c9,cb,cd,cf,d1,
  //   d3,d5,d7,d9,db,dd,df,e1,e3,e5,e7,e9,eb, ed,ef,f1,f3,f5,f7,f9,fb,fd,ff,0,0,1,1,2,2,3,3,4,4,5,
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  //   contents of ALUDH (hex, n*v repeats v):
  //   0,1,2,3,14,25,46,87,8,9,a,b,1c,2d,4e,8f,11,10,13,12,5,34,57,96,19,18,1b,1a,d,3c,5f, 9e,22,23,
  //   20,21,36,7,64,a5,2a,2b,28,29,3e,f,6c,ad,33,32,31,30,27,16,75,b4,3b,3a,39, 38,2f,1e,7d,bc,44,
  //   45,46,47,50,61,2,c3,4c,4d,4e,4f,58,69,a,cb,55,54,57,56,41,70,13, d2,5d,5c,5f,5e,49,78,1b,da,
  //   66,67,64,65,72,43,20,e1,6e,6f,6c,6d,7a,4b,28,e9,77,76, 75,74,63,52,31,f0,7f,7e,7d,7c,6b,5a,
  //   39,f8,88,89,8a,8b,9c,ad,ce,f,80,81,82,83,94,a5, c6,7,99,98,9b,9a,8d,bc,df,1e,91,90,93,92,85,
  //   b4,d7,16,aa,ab,a8,a9,be,8f,ec,2d,a2,a3, a0,a1,b6,87,e4,25,bb,ba,b9,b8,af,9e,fd,3c,b3,b2,b1,
  //   b0,a7,96,f5,34,cc,cd,ce,cf,d8, e9,8a,4b,c4,c5,c6,c7,d0,e1,82,43,dd,dc,df,de,c9,f8,9b,5a,d5,
  //   d4,d7,d6,c1,f0,93,52, ee,ef,ec,ed,fa,cb,a8,69,e6,e7,e4,e5,f2,c3,a0,61,ff,fe,fd,fc,eb,da,b9,
  //   78,f7,f6,f5, f4,e3,d2,b1,70,0,1,2,3,4,5,6,7,8,9,80,81,82,83,84,85,0,1,2,3,4,5,6,7,8,9,80,81,
  //   82, 83,84,85,0,1,2,3,4,5,6,7,8,9,80,81,82,83,84,85,0,1,2,3,4,5,6,7,8,9,80,81,82,83,84, 85,0,
  //   1,2,3,4,5,6,7,8,9,80,81,82,83,84,85,0,1,2,3,4,5,6,7,8,9,80,81,82,83,84,85,0, 1,2,3,4,5,6,7,
  //   8,9,80,81,82,83,84,85,0,1,2,3,4,5,6,7,8,9,80,81,82,83,84,85,6,7,48, 49,4a,4b,4c,4d,e,f,80,81,
  //   82,83,84,85,6,7,48,49,4a,4b,4c,4d,e,f,80,81,82,83,84,85, 6,7,48,49,4a,4b,4c,4d,e,f,80,81,82,
  //   83,84,85,6,7,48,49,4a,4b,4c,4d,e,f,80,81,82,83, 84,85,6,7,48,49,4a,4b,4c,4d,e,f,80,81,82,83,
  //   84,85,6,7,48,49,4a,4b,4c,4d,e,f,80,81, 82,83,84,85,6,7,48,49,4a,4b,4c,4d,e,f,80,81,82,83,84,
  //   85,6,7,48,49,4a,4b,4c,4d,e,f, 80,81,82,83,84,85,0,1,2,3,4,5,6,7,8,9,a,b,c,d,e,f,1,2,3,4,5,6,
  //   7,48,9,a,b,c,d,e,f, 80,2,3,4,5,6,7,48,49,a,b,c,d,e,f,80,81,3,4,5,6,7,48,49,4a,b,c,d,e,f,80,
  //   81,82,4,5, 6,7,48,49,4a,4b,c,d,e,f,80,81,82,83,5,6,7,48,49,4a,4b,4c,d,e,f,80,81,82,83,84,6,
  //   7, 48,49,4a,4b,4c,4d,e,f,80,81,82,83,84,85,7,48,49,4a,4b,4c,4d,4e,f,80,81,82,83,84,85, 86,8,
  //   9,a,b,c,d,e,f,c0,c1,c2,c3,c4,c5,c6,c7,9,a,b,c,d,e,f,80,c1,c2,c3,c4,c5,c6,c7, 88,a,b,c,d,e,f,
  //   80,81,c2,c3,c4,c5,c6,c7,88,89,b,c,d,e,f,80,81,82,c3,c4,c5,c6,c7,88, 89,8a,c,d,e,f,80,81,82,
  //   83,c4,c5,c6,c7,88,89,8a,8b,d,e,f,80,81,82,83,84,c5,c6,c7,88, 89,8a,8b,8c,e,f,80,81,82,83,84,
  //   85,c6,c7,88,89,8a,8b,8c,8d,f,80,81,82,83,84,85,86, c7,88,89,8a,8b,8c,8d,8e,0,1,2,3,4,5,6,7,
  //   8,9,a,b,c,d,e,f,8f,0,1,2,3,4,5,6,47,8,9,a, b,c,d,e,8e,8f,0,1,2,3,4,5,46,47,8,9,a,b,c,d,8d,8e,
  //   8f,0,1,2,3,4,45,46,47,8,9,a,b,c, 8c,8d,8e,8f,0,1,2,3,44,45,46,47,8,9,a,b,8b,8c,8d,8e,8f,0,1,
  //   2,43,44,45,46,47,8,9,a, 8a,8b,8c,8d,8e,8f,0,1,42,43,44,45,46,47,8,9,89,8a,8b,8c,8d,8e,8f,0,
  //   41,42,43,44,45, 46,47,8,c8,c9,ca,cb,cc,cd,ce,cf,0,1,2,3,4,5,6,7,87,c8,c9,ca,cb,cc,cd,ce,8f,
  //   0,1,2, 3,4,5,6,86,87,c8,c9,ca,cb,cc,cd,8e,8f,0,1,2,3,4,5,85,86,87,c8,c9,ca,cb,cc,8d,8e,8f, 0,
  //   1,2,3,4,84,85,86,87,c8,c9,ca,cb,8c,8d,8e,8f,0,1,2,3,83,84,85,86,87,c8,c9,ca,8b, 8c,8d,8e,8f,
  //   0,1,2,82,83,84,85,86,87,c8,c9,8a,8b,8c,8d,8e,8f,0,1,81,82,83,84,85,86, 87,c8,89,8a,8b,8c,8d,
  //   8e,8f,0,0,81,82,3,84,5,6,87,88,9,a,8b,c,8d,8e,f,0,81,82,3,84, 5,6,87,88,9,a,8b,c,8d,8e,f,0,
  //   81,82,3,84,5,6,87,88,9,a,8b,c,8d,8e,f,0,81,82,3,84,5, 6,87,88,9,a,8b,c,8d,8e,f,0,81,82,3,84,
  //   5,6,87,88,9,a,8b,c,8d,8e,f,0,81,82,3,84,5,6, 87,88,9,a,8b,c,8d,8e,f,0,81,82,3,84,5,6,87,88,
  //   9,a,8b,c,8d,8e,f,0,81,82,3,84,5,6,87, 88,9,a,8b,c,8d,8e,f,0,81,82,3,84,5,6,87,88,9,a,8b,c,8d,
  //   8e,f,0,81,82,3,84,5,6,87,88, 9,a,8b,c,8d,8e,f,0,81,82,3,84,5,6,87,88,9,a,8b,c,8d,8e,f,0,81,
  //   82,3,84,5,6,87,88,9, a,8b,c,8d,8e,f,0,81,82,3,84,5,6,87,88,9,a,8b,c,8d,8e,f,0,81,82,3,84,5,
  //   6,87,88,9,a, 8b,c,8d,8e,f,0,81,82,3,84,5,6,87,88,9,a,8b,c,8d,8e,f,0,81,82,3,84,5,6,87,88,9,
  //   a,8b, c,8d,8e,f,0,10,20,30,40,50,60,70,80,90,a0,b0,c0,d0,e0,f0,11,11,31,31,51,51,71,71, 91,
  //   91,b1,b1,d1,d1,f1,f1,20,30,20,30,60,70,60,70,a0,b0,a0,b0,e0,f0,e0,f0,31,31,31, 31,71,71,71,
  //   71,b1,b1,b1,b1,f1,f1,f1,f1,40,50,60,70,40,50,60,70,c0,d0,e0,f0,c0,d0, e0,f0,51,51,71,71,51,
  //   51,71,71,d1,d1,f1,f1,d1,d1,f1,f1,60,70,60,70,60,70,60,70,e0, f0,e0,f0,e0,f0,e0,f0,71,71,71,
  //   71,71,71,71,71,f1,f1,f1,f1,f1,f1,f1,f1,80,90,a0,b0, c0,d0,e0,f0,80,90,a0,b0,c0,d0,e0,f0,91,
  //   91,b1,b1,d1,d1,f1,f1,91,91,b1,b1,d1,d1,f1, f1,a0,b0,a0,b0,e0,f0,e0,f0,a0,b0,a0,b0,e0,f0,e0,
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  //   contents of DECODER (hex, n*v repeats v):
  //   80340051700,80340050700,80340050700,8034004f600,8034004f600,8034004ef00,8034004ef00, 8034004ee00,
  //   8034004ee00,8034004ed00,8034004ed00,8034004e700,8034004e700,8034004e200, 8034004e200,8034004e200,
  //   8034004e200,8034004de00,8034004de00,8034004de00,8034004de00, 8034004de00,8034004de00,8034004de00,
  //   8034004de00,8034004de00,8034004de00,8034004de00, 8034004de00,8034004de00,8034004de00,8034004de00,
  //   8034004de00,8034004d100,8034004d100, 8034004fb00,8034004fb00,8034004c600,8034004c600,8034004c300,
  //   8034004c300,8034004c200, 8034004c200,8034004bc00,8034004bc00,8034004b700,8034004b700,8034004b700,
  //   8034004b700, 8034004b300,8034004b300,8034004b300,8034004b300,8034004b300,8034004b300,8034004b300,
  //    8034004b300,8034004b300,8034004b300,8034004b300,8034004b300,8034004b300,8034004b300, 8034004b300,
  //   8034004b300,8034004a700,8034004a700,8034004f600,8034004f600,8034004a200, 8034004a200,8034004a100,
  //   8034004a100,80340049a00,80340049a00,80340049000,80340049000, 80340048600,80340048600,80340048600,
  //   80340048600,80340047d00,80340047d00,80340047d00, 80340047d00,80340047d00,80340047d00,80340047d00,
  //   80340047d00,80340047d00,80340047d00, 80340047d00,80340047d00,80340047d00,80340047d00,80340047d00,
  //   80340047d00,80340047300, 80340047300,8034004fb00,8034004fb00,80340046d00,80340046d00,80340046a00,
  //   80340046a00, 80340046200,80340046200,80340045700,80340045700,80340044d00,80340044d00,80340044d00,
  //    80340044d00,80340044400,80340044400,80340044400,80340044400,80340044400,80340044400, 80340044400,
  //   80340044400,80340044400,80340044400,80340044400,80340044400,80340044400, 80340044400,80340044400,
  //   80340044400,80340044000,80340044000,8034004f600,8034004f600, 80340043b00,80340043b00,80340043200,
  //   80340043200,80340043000,80340043000,80340042c00, 80340042c00,80340042700,80340042700,80340042700,
  //   80340042700,80340042300,80340042300, 80340042300,80340042300,80340042300,80340042300,80340042300,
  //   80340042300,80340042300, 80340042300,80340042300,80340042300,80340042300,80340042300,80340042300,
  //   80340042300, 80340041f00,80340041f00,8034004fb00,8034004fb00,80340041a00,80340041a00,80340041100,
  //    80340041100,80340040f00,80340040f00,80340040b00,80340040b00,80340040600,80340040600, 80340040600,
  //   80340040600,80340040200,80340040200,80340040200,80340040200,80340040200, 80340040200,80340040200,
  //   80340040200,80340040200,80340040200,80340040200,80340040200, 80340040200,80340040200,80340040200,
  //   80340040200,8034003fe00,8034003fe00,8034004f600, 8034004f600,8034003f900,8034003f900,8034003f000,
  //   8034003f000,8034003ee00,8034003ee00, 8034003ea00,8034003ea00,8034003e500,8034003e500,8034003e500,
  //   8034003e500,8034003e100, 8034003e100,8034003e100,8034003e100,8034003e100,8034003e100,8034003e100,
  //   8034003e100, 8034003e100,8034003e100,8034003e100,8034003e100,8034003e100,8034003e100,8034003e100,
  //    8034003e100,8034003dd00,8034003dd00,8034004fb00,8034004fb00,8034003d200,8034003d200, 8034003cd00,
  //   8034003cd00,8034003cc00,8034003cc00,8034003c500,8034003c500,8034003c000, 8034003c000,8034003c000,
  //   8034003c000,8034003bc00,8034003bc00,8034003bc00,8034003bc00, 8034003bc00,8034003bc00,8034003bc00,
  //   8034003bc00,8034003bc00,8034003bc00,8034003bc00, 8034003bc00,8034003bc00,8034003bc00,8034003bc00,
  //   8034003bc00,8034003b700,8034003b700, 8034004f600,8034004f600,8034003ac00,8034003ac00,8034003a800,
  //   8034003a800,80340037400, 80340037400,80340036a00,80340036a00,80340036000,80340036000,80340036000,
  //   80340036000, 80340035900,80340035900,80340035900,80340035900,80340035900,80340035900,80340035900,
  //    80340035900,80340035900,80340035900,80340035900,80340035900,80340035900,80340035900, 80340035900,
  //   80340035900,80340035500,80340035500,8034004fb00,8034004fb00,80340034a00, 80340034a00,80340034600,
  //   80340034600,80340033e00,80340033e00,80340033300,80340033300, 80340032900,80340032900,80340032900,
  //   80340032900,80340032000,80340032000,80340032000, 80340032000,80340032000,80340032000,80340032000,
  //   80340032000,80340032000,80340032000, 80340032000,80340032000,80340032000,80340032000,80340032000,
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endmodule
