// Digital circuit reg-file.dig as structural Verilog
module reg_file (
  input  CLK,
  input  [7:0] D,
  input  [3:0] RS,
  input  LE,
  output [7:0] Q
);

  RAMDualPort #(.AddrBits(4), .Bits(8)) RF (.A(RS), .Din(D), .str(LE), .C(CLK), .ld(1'b1), .D(Q));
endmodule
